# Fritzing sketch schematic (saved by Fritzing 0.9.3b)
circuit board: 8.46667cm x 5.64444cm

parts:
  Part1 = Arduino Nano (Rev3.0)
  JP1 = Header 6 [package=1x06-smd]
  JP2 = Header 6 [package=1x06-smd]

nets:
  N1: Part1.D4, JP2.3
  N2: Part1.D5, JP2.2
  N3: Part1.D6, JP2.1
  N4: Part1.D7, JP1.3
  N5: Part1.D8, JP1.2
  N6: Part1.D9, JP1.1
  N7: Part1.GND, JP1.4, JP2.4
  N8: Part1.3V3, JP1.6, JP2.6
